// Logisim project B1_Group3_FP_Adder.circ as structural Verilog: 2 circuits, main circuit main
module main (
  input  [15:0] B,
  input  [15:0] A,
  output [3:0] out_3,
  output [1:0] out_4,
  output [12:0] out_5,
  output out_6,
  output [3:0] out_7,
  output [11:0] out_8,
  output [12:0] out_9,
  output [3:0] out_10,
  output [11:0] out_11,
  output [11:0] out_12,
  output [11:0] out_13,
  output [3:0] out_14,
  output [11:0] out_15,
  output [15:0] Output,
  output Underflow,
  output Overflow
);

  wire adder_4_cout, and_1_out, and_2_out, comparator_1_lt, comparator_2_lt, comparator_4_eq,
       comparator_4_gt, multiplexer_9_out, multiplexer_10_out, multiplexer_11_out, multiplexer_12_out,
       multiplexer_15_out, not_1_out, or_2_out, xor_9_out;
  wire [3:0] adder_2_out, adder_3_out, bitfinder_1_index, multiplexer_1_out, subtractor_1_out, xor_5_out;
  wire [11:0] bit_extender_1_out, bit_extender_3_out, multiplexer_4_out, multiplexer_6_out, negator_1_out,
       negator_2_out, shifter_1_out, shifter_2_out;
  wire [12:0] bit_extender_2_out;
  wire [12:12] multiplexer_6_out_2;

  Comparator #(.width(4), .mode("unsigned")) comparator_1 (
    .a(multiplexer_1_out), .b(out_14), .lt(comparator_1_lt));  // open: gt, eq
  or or_1 (Underflow, comparator_1_lt, comparator_2_lt);
  Multiplexer #(.width(4), .enable("false")) multiplexer_1 (
    .in0(B[14:11]), .in1(A[14:11]), .out(multiplexer_1_out), .sel(out_6));
  Subtractor #(.width(4)) subtractor_1 (.a(multiplexer_1_out), .b(out_14), .out(subtractor_1_out));  // open: bin, bout
  Subtractor #(.width(4)) subtractor_2 (.a(4'b1011), .b(bitfinder_1_index), .out(out_14));  // open: bin, bout
  Multiplexer #(.width(4), .enable("false")) multiplexer_2 (
    .in0(subtractor_1_out), .in1(adder_2_out), .out(Output[14:11]), .sel(and_1_out));
  Adder #(.width(4)) adder_1 (.a(A[14:11]), .b(out_3), .out(out_7), .cin(1'b1), .cout(out_6));
  Adder #(.width(4)) adder_2 (.a(multiplexer_1_out), .b(4'b0001), .out(adder_2_out));  // open: cin, cout
  xor xor_1 (out_3[0], 1'b1, B[11]);
  xor xor_2 (out_3[1], 1'b1, B[12]);
  xor xor_3 (out_3[2], 1'b1, B[13]);
  xor xor_4 (out_3[3], 1'b1, B[14]);
  BitFinder #(.width(12), .\type ("high1")) bitfinder_1 (
    .in(multiplexer_4_out), .index(bitfinder_1_index));  // open: found
  Shifter #(.width(12)) shifter_1 (.in(multiplexer_4_out), .\dist (out_14), .out(shifter_1_out));
  Comparator #(.width(4), .mode("unsigned")) comparator_2 (
    .a(Output[14:11]), .b(4'b0001), .lt(comparator_2_lt));  // open: gt, eq
  assign bit_extender_1_out = {{1{1'b1}}, A[10:0]};  // Bit_Extender bit_extender_1
  xor xor_5 (xor_5_out[0], 1'b1, out_7[0]);
  xor xor_6 (xor_5_out[1], 1'b1, out_7[1]);
  xor xor_7 (xor_5_out[2], 1'b1, out_7[2]);
  xor xor_8 (xor_5_out[3], 1'b1, out_7[3]);
  Multiplexer #(.width(12), .enable("false")) multiplexer_3 (
    .in0(shifter_1_out), .in1(shifter_2_out), .out(out_15), .sel(and_1_out));
  Multiplexer #(.width(12), .enable("false")) multiplexer_4 (
    .in0(out_11), .in1(negator_1_out), .out(multiplexer_4_out), .sel(and_2_out));
  and and_1 (and_1_out, adder_4_cout, not_1_out);
  Comparator #(.width(4), .mode("unsigned")) comparator_3 (
    .a(4'b1110), .b(Output[14:11]), .lt(Overflow));  // open: gt, eq
  Multiplexer #(.width(13), .enable("false")) multiplexer_5 (
    .in0({B[15], bit_extender_3_out}), .in1({A[15], bit_extender_1_out}), .out(out_5), .sel(out_6));
  Adder #(.width(4)) adder_3 (.a(xor_5_out), .b(4'b0000), .out(adder_3_out), .cin(1'b1));  // open: cout
  Shifter #(.width(12), .shift("lr")) shifter_2 (.in(multiplexer_4_out), .\dist (4'b0001), .out(shifter_2_out));
  not not_1 (not_1_out, xor_9_out);
  Multiplexer #(.width(13), .enable("false")) multiplexer_6 (
    .in0({A[15], bit_extender_1_out}), .in1({B[15], bit_extender_3_out}),
    .out({multiplexer_6_out_2[12], multiplexer_6_out}), .sel(out_6));
  assign bit_extender_2_out = {{1{1'b0}}, multiplexer_6_out};  // Bit_Extender bit_extender_2
  Multiplexer #(.width(4), .enable("false")) multiplexer_7 (.in0(adder_3_out), .in1(out_7), .out(out_10), .sel(out_6));
  Negator #(.width(12)) negator_1 (.in(out_11), .out(negator_1_out));
  Shifter #(.width(13), .shift("lr")) shifter_3 (.in(bit_extender_2_out), .\dist (out_10), .out(out_9));
  assign bit_extender_3_out = {{1{1'b1}}, B[10:0]};  // Bit_Extender bit_extender_3
  Adder #(.width(12)) adder_4 (.a(out_12), .b(out_13), .out(out_11), .cout(adder_4_cout));  // open: cin
  Multiplexer #(.width(12), .enable("false")) multiplexer_8 (
    .in0(out_5[11:0]), .in1(negator_2_out), .out(out_12), .sel(multiplexer_10_out));
  Negator #(.width(12)) negator_2 (.in(out_5[11:0]), .out(negator_2_out));
  and and_2 (and_2_out, Output[15], xor_9_out);
  xor xor_9 (xor_9_out, A[15], B[15]);
  Multiplexer #(.enable("false")) multiplexer_9 (.in0(B[15]), .in1(A[15]), .out(multiplexer_9_out), .sel(out_6));
  Multiplexer #(.enable("false")) multiplexer_10 (
    .in0(1'b0), .in1(multiplexer_9_out), .out(multiplexer_10_out), .sel(xor_9_out));
  Multiplexer #(.enable("false")) multiplexer_11 (.in0(A[15]), .in1(B[15]), .out(multiplexer_11_out), .sel(out_6));
  Multiplexer #(.enable("false")) multiplexer_12 (
    .in0(1'b0), .in1(multiplexer_11_out), .out(multiplexer_12_out), .sel(xor_9_out));
  Negator #(.width(12)) negator_3 (.in(out_9[11:0]), .out(out_8));
  Multiplexer #(.width(12), .enable("false")) multiplexer_13 (
    .in0(out_9[11:0]), .in1(out_8), .out(out_13), .sel(multiplexer_12_out));
  Multiplexer #(.select(2), .enable("false")) multiplexer_14 (
    .in0(1'b0), .in1(multiplexer_15_out), .in2(multiplexer_15_out), .in3(1'b1), .out(Output[15]),
    .sel({A[15], B[15]}));
  Multiplexer #(.enable("false")) multiplexer_15 (
    .in0(multiplexer_6_out_2[12]), .in1(out_5[12]), .out(multiplexer_15_out), .sel(or_2_out));
  Comparator #(.width(12), .mode("unsigned")) comparator_4 (
    .a(out_5[11:0]), .b(out_9[11:0]), .gt(comparator_4_gt), .eq(comparator_4_eq));  // open: lt
  or or_2 (or_2_out, comparator_4_gt, comparator_4_eq);

  assign out_4 = {A[15], B[15]};
  assign Output[10:0] = out_15[10:0];

  // Notes on the sheet:
  //   Sign(A)
  //   Maximum Exponent
  //   of 2 inputs
  //   Decreament
  //   Exponent(A)
  //   Determining Exponent from the below mux
  //   Increament
  //   Index of Highest order 1
  //   Subtractor gives
  //   amount of
  //   decreament
  //   Left Shift
  //   Fraction(A)
  //   Right Shift
  //   Sign bit is added 
  //   Larger
  //   Sign(B)
  //   Exponent(B)
  //   Smaller
  //   If Cout is 1 and both signs are not same
  //   then right shift of fraction is needed
  //   and exponent is increased by 1
  //   Fraction(B)
  //   Extract sign bit
  //   of smaller exponent
  //   for computing sign
  //   Sign bit is added 
  //   Addition Result
  //   If both signs are
  //   same,mux
  //   gives 0
  //   If both signs are not same,
  //   and output's sign is 1
  //   2's compl. is required
  //   If both signs are same
  //   then ignore negator
  //   else mux gives sign
  //   of larger exponent
  //   else mux gives sign
  //   of smaller exponent
  //   Sign(A)
  //   Sign(B)
  //   fraction(larger)
  //   fraction(smaller)
  //   Sign
  //   (Smaller)
  //   Sign
  //   (Larger)
endmodule

module Block_Diagram (
  input  [15:0] A,
  input  [15:0] B,
  output Overflow,
  output Underflow,
  output [15:0] Output
);

  main main_1 (
    .A(A), .B(B), .Underflow(Underflow), .Output(Output), .Overflow(Overflow));  // open: out_3, out_6, out_7, out_12, out_13, out_5, out_11, out_14, out_15, out_10, out_9, out_4, out_8
endmodule
