// Logisim project FP_Adder.circ as structural Verilog: 1 circuit, main circuit main
module main (
  input  [15:0] B,
  input  [15:0] A,
  input  [3:0] in_3,
  input  [3:0] in_4,
  input  [3:0] in_5,
  input  [3:0] Increament,
  input  [3:0] in_7,
  input  [3:0] in_8,
  output [3:0] out_9,
  output [1:0] out_10,
  output [12:0] out_11,
  output out_12,
  output [3:0] out_13,
  output [11:0] out_14,
  output [12:0] out_15,
  output [3:0] out_16,
  output [11:0] out_17,
  output [11:0] out_18,
  output [11:0] out_19,
  output [3:0] out_20,
  output [11:0] out_21,
  output [15:0] out_22,
  output Underflow,
  output Overflow
);

  wire adder_4_cout, and_1_out, comparator_1_lt, comparator_2_lt, comparator_4_eq, comparator_4_gt,
       multiplexer_9_out, multiplexer_10_out, multiplexer_11_out, multiplexer_12_out, multiplexer_15_out,
       or_2_out, xor_9_out;
  wire [3:0] adder_1_out, adder_3_out, bitfinder_1_index, multiplexer_1_out, subtractor_1_out, xor_5_out;
  wire [11:0] bit_extender_1_out, bit_extender_3_out, multiplexer_4_out, multiplexer_6_out, negator_1_out,
       negator_2_out, shifter_1_out, shifter_2_out;
  wire [12:0] bit_extender_2_out;
  wire [12:12] multiplexer_6_out_2;

  Comparator #(.width(4), .mode("unsigned")) comparator_1 (
    .a(multiplexer_1_out), .b(out_20), .lt(comparator_1_lt));  // open: gt, eq
  or or_1 (Underflow, comparator_1_lt, comparator_2_lt);
  Multiplexer #(.width(4), .enable("false")) multiplexer_1 (
    .in0(B[14:11]), .in1(A[14:11]), .out(multiplexer_1_out), .sel(out_12));
  Subtractor #(.width(4)) subtractor_1 (.a(multiplexer_1_out), .b(out_20), .out(subtractor_1_out));  // open: bin, bout
  Subtractor #(.width(4)) subtractor_2 (.a(in_5), .b(bitfinder_1_index), .out(out_20));  // open: bin, bout
  Adder #(.width(4)) adder_1 (.a(multiplexer_1_out), .b(Increament), .out(adder_1_out));  // open: cin, cout
  Multiplexer #(.width(4), .enable("false")) multiplexer_2 (
    .in0(subtractor_1_out), .in1(adder_1_out), .out(out_22[14:11]), .sel(adder_4_cout));
  Adder #(.width(4)) adder_2 (.a(A[14:11]), .b(out_9), .out(out_13), .cin(1'b1), .cout(out_12));
  xor xor_1 (out_9[0], 1'b1, B[11]);
  xor xor_2 (out_9[1], 1'b1, B[12]);
  xor xor_3 (out_9[2], 1'b1, B[13]);
  xor xor_4 (out_9[3], 1'b1, B[14]);
  BitFinder #(.width(12), .\type ("high1")) bitfinder_1 (
    .in(multiplexer_4_out), .index(bitfinder_1_index));  // open: found
  Shifter #(.width(12)) shifter_1 (.in(multiplexer_4_out), .\dist (out_20), .out(shifter_1_out));
  Comparator #(.width(4), .mode("unsigned")) comparator_2 (
    .a(out_22[14:11]), .b(in_8), .lt(comparator_2_lt));  // open: gt, eq
  assign bit_extender_1_out = {{1{1'b1}}, A[10:0]};  // Bit_Extender bit_extender_1
  xor xor_5 (xor_5_out[0], 1'b1, out_13[0]);
  xor xor_6 (xor_5_out[1], 1'b1, out_13[1]);
  xor xor_7 (xor_5_out[2], 1'b1, out_13[2]);
  xor xor_8 (xor_5_out[3], 1'b1, out_13[3]);
  Multiplexer #(.width(12), .enable("false")) multiplexer_3 (
    .in0(shifter_1_out), .in1(shifter_2_out), .out(out_21), .sel(adder_4_cout));
  Multiplexer #(.width(12), .enable("false")) multiplexer_4 (
    .in0(out_17), .in1(negator_1_out), .out(multiplexer_4_out), .sel(and_1_out));
  Comparator #(.width(4), .mode("unsigned")) comparator_3 (.a(in_7), .b(out_22[14:11]), .lt(Overflow));  // open: gt, eq
  Multiplexer #(.width(13), .enable("false")) multiplexer_5 (
    .in0({B[15], bit_extender_3_out}), .in1({A[15], bit_extender_1_out}), .out(out_11), .sel(out_12));
  Adder #(.width(4)) adder_3 (.a(xor_5_out), .b(in_3), .out(adder_3_out), .cin(1'b1));  // open: cout
  Shifter #(.width(12), .shift("lr")) shifter_2 (.in(multiplexer_4_out), .\dist (in_4), .out(shifter_2_out));
  Multiplexer #(.width(13), .enable("false")) multiplexer_6 (
    .in0({A[15], bit_extender_1_out}), .in1({B[15], bit_extender_3_out}),
    .out({multiplexer_6_out_2[12], multiplexer_6_out}), .sel(out_12));
  assign bit_extender_2_out = {{1{1'b0}}, multiplexer_6_out};  // Bit_Extender bit_extender_2
  Multiplexer #(.width(4), .enable("false")) multiplexer_7 (
    .in0(adder_3_out), .in1(out_13), .out(out_16), .sel(out_12));
  Negator #(.width(12)) negator_1 (.in(out_17), .out(negator_1_out));
  Shifter #(.width(13), .shift("lr")) shifter_3 (.in(bit_extender_2_out), .\dist (out_16), .out(out_15));
  assign bit_extender_3_out = {{1{1'b1}}, B[10:0]};  // Bit_Extender bit_extender_3
  Adder #(.width(12)) adder_4 (.a(out_18), .b(out_19), .out(out_17), .cout(adder_4_cout));  // open: cin
  Multiplexer #(.width(12), .enable("false")) multiplexer_8 (
    .in0(out_11[11:0]), .in1(negator_2_out), .out(out_18), .sel(multiplexer_10_out));
  Negator #(.width(12)) negator_2 (.in(out_11[11:0]), .out(negator_2_out));
  and and_1 (and_1_out, out_22[15], xor_9_out);
  xor xor_9 (xor_9_out, A[15], B[15]);
  Multiplexer #(.enable("false")) multiplexer_9 (.in0(B[15]), .in1(A[15]), .out(multiplexer_9_out), .sel(out_12));
  Multiplexer #(.enable("false")) multiplexer_10 (
    .in0(1'b0), .in1(multiplexer_9_out), .out(multiplexer_10_out), .sel(xor_9_out));
  Multiplexer #(.enable("false")) multiplexer_11 (.in0(A[15]), .in1(B[15]), .out(multiplexer_11_out), .sel(out_12));
  Multiplexer #(.enable("false")) multiplexer_12 (
    .in0(1'b0), .in1(multiplexer_11_out), .out(multiplexer_12_out), .sel(xor_9_out));
  Negator #(.width(12)) negator_3 (.in(out_15[11:0]), .out(out_14));
  Multiplexer #(.width(12), .enable("false")) multiplexer_13 (
    .in0(out_15[11:0]), .in1(out_14), .out(out_19), .sel(multiplexer_12_out));
  Multiplexer #(.select(2), .enable("false")) multiplexer_14 (
    .in0(1'b0), .in1(multiplexer_15_out), .in2(multiplexer_15_out), .in3(1'b1), .out(out_22[15]),
    .sel({A[15], B[15]}));
  Multiplexer #(.enable("false")) multiplexer_15 (
    .in0(multiplexer_6_out_2[12]), .in1(out_11[12]), .out(multiplexer_15_out), .sel(or_2_out));
  Comparator #(.width(12), .mode("unsigned")) comparator_4 (
    .a(out_11[11:0]), .b(out_15[11:0]), .gt(comparator_4_gt), .eq(comparator_4_eq));  // open: lt
  or or_2 (or_2_out, comparator_4_gt, comparator_4_eq);

  assign out_10 = {A[15], B[15]};
  assign out_22[10:0] = out_21[10:0];

  // Notes on the sheet:
  //   Sign(A)
  //   Maximum Exponent
  //   of 2 inputs
  //   Decreament
  //   Exponent(A)
  //   Determining Exponent from the below mux
  //   Index of Highest order 1
  //   Subtractor gives
  //   amount of
  //   decreament
  //   Left Shift
  //   Fraction(A)
  //   Determining Fraction from the below mux
  //   Right Shift
  //   Sign bit is added 
  //   Larger
  //   If Cout  is 1
  //   Sign(B)
  //   Exponent(B)
  //   Smaller
  //   then right shift of fraction is needed
  //   and exponent is increased by 1
  //   Fraction(B)
  //   Extract sign bit
  //   of smaller exponent
  //   for computing sign
  //   Sign bit is added 
  //   Addition Result
  //   If both signs are
  //   same,mux
  //   gives 0
  //   If both signs are same
  //   then ignore negator
  //   else mux gives sign
  //   of larger exponent
  //   else mux gives sign
  //   of smaller exponent
endmodule
