// Logisim project B1_Group_05.circ as structural Verilog: 2 circuits, main circuit main
module main (
  input  [2:0] S2_S1_S0,
  input  [3:0] A,
  input  [3:0] B,
  output [3:0] ZSOC,
  output [3:0] Output,
  output Cout
);

  wire adder_1_cout, adder_2_cout, adder_3_cout, adder_4_cout, and_1_out, and_2_out, and_3_out, and_4_out,
       and_5_out, and_6_out, and_7_out, and_8_out, and_9_out, and_10_out, and_11_out, and_12_out, not_1_out,
       not_2_out, not_3_out, not_4_out, not_5_out, or_1_out, or_2_out, or_3_out, or_4_out, xnor_1_out,
       xor_1_out, xor_2_out, xor_3_out, xor_4_out, xor_5_out;

  xnor xnor_1 (xnor_1_out, S2_S1_S0[2], S2_S1_S0[0]);
  xor xor_1 (xor_1_out, S2_S1_S0[2], B[0]);
  not not_1 (not_1_out, B[0]);
  xor xor_2 (xor_2_out, S2_S1_S0[2], B[1]);
  not not_2 (not_2_out, B[1]);
  xor xor_3 (xor_3_out, S2_S1_S0[2], B[2]);
  not not_3 (not_3_out, B[2]);
  xor xor_4 (xor_4_out, S2_S1_S0[2], B[3]);
  not not_4 (not_4_out, B[3]);
  and and_1 (and_1_out, S2_S1_S0[0], xor_1_out);
  and and_2 (and_2_out, S2_S1_S0[0], xor_2_out);
  and and_3 (and_3_out, S2_S1_S0[0], xor_3_out);
  and and_4 (and_4_out, S2_S1_S0[0], xor_4_out);
  or or_1 (or_1_out, and_1_out, A[0]);
  and and_5 (and_5_out, not_1_out, xnor_1_out);
  or or_2 (or_2_out, and_2_out, A[1]);
  and and_6 (and_6_out, not_2_out, xnor_1_out);
  or or_3 (or_3_out, and_3_out, A[2]);
  and and_7 (and_7_out, not_3_out, xnor_1_out);
  or or_4 (or_4_out, and_4_out, A[3]);
  and and_8 (and_8_out, not_4_out, xnor_1_out);
  not not_5 (not_5_out, S2_S1_S0[0]);
  and and_9 (and_9_out, not_5_out, S2_S1_S0[1]);
  and and_10 (and_10_out, not_5_out, adder_1_cout);
  and and_11 (and_11_out, not_5_out, adder_2_cout);
  and and_12 (and_12_out, not_5_out, adder_3_cout);
  and and_13 (Cout, not_5_out, adder_4_cout);
  Adder #(.width(1)) adder_1 (.a(or_1_out), .b(and_5_out), .out(Output[0]), .cin(and_9_out), .cout(adder_1_cout));
  Adder #(.width(1)) adder_2 (.a(or_2_out), .b(and_6_out), .out(Output[1]), .cin(and_10_out), .cout(adder_2_cout));
  Adder #(.width(1)) adder_3 (.a(or_3_out), .b(and_7_out), .out(Output[2]), .cin(and_11_out), .cout(adder_3_cout));
  Adder #(.width(1)) adder_4 (.a(or_4_out), .b(and_8_out), .out(Output[3]), .cin(and_12_out), .cout(adder_4_cout));
  and and_14 (ZSOC[0], not_5_out, Cout);
  xor xor_5 (xor_5_out, and_12_out, Cout);
  and and_15 (ZSOC[1], not_5_out, xor_5_out);
  nor nor_1 (ZSOC[3], Output[3], Output[2], Output[1], Output[0]);

  assign ZSOC[2] = Output[3];

  // Notes on the sheet:
  //   S2
  //   S2⊙S0
  //   A0
  //   B0
  //   A1
  //   B1
  //   A2
  //   B2
  //   A3
  //   B3
  //   S0
  //   S1
  //   S0'
  //   A0+S0(S2⊕B0)
  //   (S2⊙S0)B0'
  //   A1+S0(S2⊕B1)
  //   (S2⊙S0)B1'
  //   A2+S0(S2⊕B2)
  //   (S2⊙S0)B2'
  //   A3+S0(S2⊕B3)
  //   (S2⊙S0)B3'
  //   Cin(S1)
  //   C0
  //   C1
  //   C2
  //   C3
  //   C4
  //   SF
  //   CF
  //   OF
  //   ZF
endmodule

module Circuit_diagram (
  input  [2:0] S2_S1_S0,
  input  [3:0] A,
  input  [3:0] B,
  output Cout,
  output [3:0] ZSOC,
  output [3:0] Output
);

  main _4_bit_ALU (.S2_S1_S0(S2_S1_S0), .A(A), .B(B), .Cout(Cout), .ZSOC(ZSOC), .Output(Output));
endmodule
