// Logisim project Full_Adder_Group_05_updated.circ as structural Verilog: 8 circuits, main circuit main
module main (
  input  [15:0] Input_A,
  input  [15:0] Input_B,
  output Overflow,
  output [15:0] Output_A_B,
  output Underflow
);

  Floating_Point_Adder _16_bit_FP_Adder (
    .Output(Output_A_B), .Input_A(Input_B), .Input_B(Input_A), .Underflow(Underflow), .Overflow(Overflow));
endmodule

module Exponent_Subtractor (
  input  [3:0] A,
  input  [3:0] B,
  output [3:0] E1___E2,
  output E1____E2
);

  wire [3:0] _4_bit_ALU_2_output, _4_bit_ALU_output;
  wire [3:1] _4_bit_ALU_2_zsoc;

  B1_Group_05_main _4_bit_ALU (.S2_S1_S0(3'b010), .A(B), .B(A), .Output(_4_bit_ALU_output));  // open: Cout, ZSOC
  B1_Group_05_main _4_bit_ALU_2 (
    .S2_S1_S0(3'b010), .A(A), .B(B), .ZSOC({_4_bit_ALU_2_zsoc, E1____E2}), .Output(_4_bit_ALU_2_output));  // open: Cout
  Multiplexer #(.width(4), .enable("false")) multiplexer_1 (
    .in0(_4_bit_ALU_output), .in1(_4_bit_ALU_2_output), .out(E1___E2), .sel(E1____E2));

  // Notes on the sheet:
  //   A-B is selected by the MUX when A>=B, and B-A is selected when A<B.
  //   2 i.e. 010 is the selection bit for subtraction for this 4-bit ALU
  //   Takes the exponents of the two FP numbers as input and outputs their difference, and indicates which exponent is the bigger one.
  //   Two ALU's are necessary to display the absolute difference between the two exponenets. We need a non-negative value to shift the fraction.
endmodule

module Normaliser (
  input  [12:0] Significand,
  input  [3:0] Exponent,
  output [10:0] Fraction,
  output Underflow,
  output Overflow,
  output [3:0] Exponent_2
);

  wire _4_bit_ALU_3_cout, and_1_out, bitselector_1_out, not_1_out;
  wire [3:0] _4_bit_ALU_2_output, _4_bit_ALU_3_output, _4_bit_ALU_output, bitfinder_1_index;
  wire [10:0] bit_extender_1_out, bit_extender_2_out;
  wire [12:0] shifter_1_out, shifter_2_out;

  BitSelector #(.width(13)) bitselector_1 (.in(Significand), .out(bitselector_1_out), .sel(4'b1100));
  BitFinder #(.width(13), .\type ("high1")) bitfinder_1 (.in(Significand), .index(bitfinder_1_index));  // open: found
  Shifter #(.width(13), .shift("lr")) shifter_1 (.in(Significand), .\dist (4'b0001), .out(shifter_1_out));
  Bit_Extender #(.in_width(13), .out_width(11)) bit_extender_1 (.in(shifter_1_out), .out(bit_extender_1_out));
  Circuit_diagram _4_bit_ALU (.S2_S1_S0(3'b110), .A(Exponent), .Output(_4_bit_ALU_output));  // open: B, Cout, ZSOC
  Circuit_diagram _4_bit_ALU_2 (
    .S2_S1_S0(3'b010), .A(4'b1011), .B(bitfinder_1_index), .Output(_4_bit_ALU_2_output));  // open: Cout, ZSOC
  Shifter #(.width(13)) shifter_2 (.in(Significand), .\dist (_4_bit_ALU_2_output), .out(shifter_2_out));
  Circuit_diagram _4_bit_ALU_3 (
    .S2_S1_S0(3'b010), .A(Exponent), .B(_4_bit_ALU_2_output), .Cout(_4_bit_ALU_3_cout),
    .Output(_4_bit_ALU_3_output));  // open: ZSOC
  Bit_Extender #(.in_width(13), .out_width(11)) bit_extender_2 (.in(shifter_2_out), .out(bit_extender_2_out));
  and and_1 (and_1_out, _4_bit_ALU_output[0], _4_bit_ALU_output[1], _4_bit_ALU_output[2], _4_bit_ALU_output[3]);
  not not_1 (not_1_out, _4_bit_ALU_3_cout);
  Multiplexer #(.width(11), .enable("false")) multiplexer_1 (
    .in0(bit_extender_2_out), .in1(bit_extender_1_out), .out(Fraction), .sel(bitselector_1_out));
  Multiplexer #(.enable("false")) multiplexer_2 (.in0(not_1_out), .in1(1'b0), .out(Underflow), .sel(bitselector_1_out));
  Multiplexer #(.enable("false")) multiplexer_3 (.in0(1'b0), .in1(and_1_out), .out(Overflow), .sel(bitselector_1_out));
  Multiplexer #(.width(4), .enable("false")) multiplexer_4 (
    .in0(_4_bit_ALU_3_output), .in1(_4_bit_ALU_output), .out(Exponent_2), .sel(bitselector_1_out));

  // Notes on the sheet:
  //   For this reason, an underflow flag is kept to indicate expoent underflow during subtraction of the exponent.
  //   Shifter
  //   exponent) to select the appropriate output. If the MSB of the signifcand i.e. 12-th bit is 1 then the significand needs to normalized by rignt shifting 1-bit, and the exponent needs to be incremented.
  //   So the lower part is selected. If MSB of the significand is 0, then it may be normalized by right shifting (n-1) bits, where n is the position of the first 1 from the left, (n-1) is also subtracted from the exponent.
  //   So the upper part is selected by the two MUXs. Now during subtraction of the exponent, A<B may occur in the 4-bit ALU. This would mean a negative exponent which is underflow in case of biased exponent.
  //   Shifter
  //   This circuit normalizes and truncates the output. The upper part normalizes the significand by left shifitng, and the lower part normalizes by right shifting. Then two MUXs are used (one for signifcand and other for
endmodule

module Floating_Point_Adder (
  input  [15:0] Input_A,
  input  [15:0] Input_B,
  output Overflow,
  output [15:0] Output,
  output Underflow
);

  wire bitselector_1_out, exponent_subtractor_1_e1____e2, multiplexer_3_out, multiplexer_5_out, nor_1_out,
       normaliser_1_underflow, not_1_out, separator_2_sign_bit, Sign_A;
  wire [3:0] exponent_subtractor_1_e1___e2, multiplexer_1_out, normaliser_1_exponent_2, separator_1_exponent,
       separator_2_exponent;
  wire [10:0] normaliser_1_fraction, separator_1_fraction, separator_2_fraction;
  wire [11:0] bit_extender_1_out, bit_extender_2_out, multiplexer_2_out, multiplexer_4_out, shifter_1_out;
  wire [12:0] bit_extender_3_out, n13_bit_2_s_complementer_1_output;
  wire [13:0] adder_1_out, n12_bit_2_s_complementer_1_output, n12_bit_2_s_complementer_2_output;

  Separator separator_1 (
    ._16_bit_Input(Input_A), .Sign_bit(Sign_A), .Exponent(separator_1_exponent),
    .Fraction(separator_1_fraction));
  Exponent_Subtractor exponent_subtractor_1 (
    .A(separator_2_exponent), .B(separator_1_exponent), .E1___E2(exponent_subtractor_1_e1___e2),
    .E1____E2(exponent_subtractor_1_e1____e2));
  Multiplexer #(.width(4), .enable("false")) multiplexer_1 (
    .in0(separator_1_exponent), .in1(separator_2_exponent), .out(multiplexer_1_out),
    .sel(exponent_subtractor_1_e1____e2));
  assign bit_extender_1_out = {{1{1'b1}}, separator_1_fraction};  // Bit_Extender bit_extender_1
  not not_1 (not_1_out, exponent_subtractor_1_e1____e2);
  Multiplexer #(.width(12), .enable("false")) multiplexer_2 (
    .in0(bit_extender_1_out), .in1(bit_extender_2_out), .out(multiplexer_2_out), .sel(not_1_out));
  Shifter #(.width(12), .shift("lr")) shifter_1 (
    .in(multiplexer_2_out), .\dist (exponent_subtractor_1_e1___e2), .out(shifter_1_out));
  Separator separator_2 (
    ._16_bit_Input(Input_B), .Sign_bit(separator_2_sign_bit), .Exponent(separator_2_exponent),
    .Fraction(separator_2_fraction));
  Multiplexer #(.enable("false")) multiplexer_3 (
    .in0(Sign_A), .in1(separator_2_sign_bit), .out(multiplexer_3_out), .sel(not_1_out));
  _12_bit_2_s_complementer u_12_bit_2_s_complementer_1 (
    .Cin(multiplexer_3_out), .A(shifter_1_out), .Output(n12_bit_2_s_complementer_1_output));
  assign bit_extender_2_out = {{1{1'b1}}, separator_2_fraction};  // Bit_Extender bit_extender_2
  Multiplexer #(.width(12), .enable("false")) multiplexer_4 (
    .in0(bit_extender_1_out), .in1(bit_extender_2_out), .out(multiplexer_4_out),
    .sel(exponent_subtractor_1_e1____e2));
  Multiplexer #(.enable("false")) multiplexer_5 (
    .in0(Sign_A), .in1(separator_2_sign_bit), .out(multiplexer_5_out), .sel(exponent_subtractor_1_e1____e2));
  _12_bit_2_s_complementer u_12_bit_2_s_complementer_2 (
    .Cin(multiplexer_5_out), .A(multiplexer_4_out), .Output(n12_bit_2_s_complementer_2_output));
  Bit_Extender #(.in_width(14), .out_width(13)) bit_extender_3 (.in(adder_1_out), .out(bit_extender_3_out));
  Adder #(.width(14)) adder_1 (
    .a(n12_bit_2_s_complementer_1_output), .b(n12_bit_2_s_complementer_2_output), .out(adder_1_out));  // open: cin, cout
  _13_bit_2_s_complementer u_13_bit_2_s_complementer_1 (
    .Cin(bitselector_1_out), .A(bit_extender_3_out), .Output(n13_bit_2_s_complementer_1_output));
  BitSelector #(.width(14)) bitselector_1 (.in(adder_1_out), .out(bitselector_1_out), .sel(4'b1101));
  Normaliser normaliser_1 (
    .Significand(n13_bit_2_s_complementer_1_output), .Exponent(multiplexer_1_out),
    .Fraction(normaliser_1_fraction), .Underflow(normaliser_1_underflow),
    .Exponent_2(normaliser_1_exponent_2), .Overflow(Overflow));
  Merger merger_1 (
    ._16_bit_Output(Output), .Sign_bit(bitselector_1_out), .Exponent(normaliser_1_exponent_2),
    .Fraction(normaliser_1_fraction));
  nor nor_1 (nor_1_out, normaliser_1_exponent_2[0], normaliser_1_exponent_2[1], normaliser_1_exponent_2[2], normaliser_1_exponent_2[3]);
  or or_1 (Underflow, normaliser_1_underflow, nor_1_out);

  // Notes on the sheet:
  //   Exponent
  //   Sign bit
  //   Fraction
  //   Shifter
endmodule

module Separator (
  input  [15:0] _16_bit_Input,
  output [10:0] Fraction,
  output [3:0] Exponent,
  output Sign_bit
);


  assign Exponent = _16_bit_Input[14:11];
  assign Fraction = _16_bit_Input[10:0];
  assign Sign_bit = _16_bit_Input[15];

  // Notes on the sheet:
  //   Separates sign bit, exponent and fraction from the 16-bit input.
endmodule

module Merger (
  input  [10:0] Fraction,
  input  [3:0] Exponent,
  input  Sign_bit,
  output [15:0] _16_bit_Output
);


  assign _16_bit_Output = {Sign_bit, Exponent, Fraction};

  // Notes on the sheet:
  //   Merges sign bit, fraction and exponent into 16-bit output.
endmodule

module _13_bit_2_s_complementer (
  input  Cin,
  input  [12:0] A,
  output [12:0] Output
);

  wire [12:0] bit_extender_1_out, xor_1_out;

  assign bit_extender_1_out = {{12{Cin}}, Cin};  // Bit_Extender bit_extender_1
  assign xor_1_out = bit_extender_1_out ^ A;  // XOR_Gate xor_1, 13 bits wide
  Adder #(.width(13)) adder_1 (.a({13{1'b0}}), .b(xor_1_out), .out(Output), .cin(Cin));  // open: cout

  // Notes on the sheet:
  //   Works in a similar way to the 12-bit 2's complementer, minus the sign extension part. This circuit takes a 13-bit input A and a sign bit Cin, and outputs the 2's complement of A.
  //   This is necessary because in IEEE-754 standard, fractions of the negative numbers are not stored in 2's complement form. So we need to show the actual fraction in case of negative numbers.
endmodule

module _12_bit_2_s_complementer (
  input  Cin,
  input  [11:0] A,
  output [13:0] Output
);

  wire [11:0] adder_1_out, bit_extender_1_out, xor_1_out;

  assign bit_extender_1_out = {{11{Cin}}, Cin};  // Bit_Extender bit_extender_1
  assign xor_1_out = bit_extender_1_out ^ A;  // XOR_Gate xor_1, 12 bits wide
  Adder #(.width(12)) adder_1 (.a({12{1'b0}}), .b(xor_1_out), .out(adder_1_out), .cin(Cin));  // open: cout
  assign Output = {{2{Cin}}, adder_1_out};  // Bit_Extender bit_extender_2

  // Notes on the sheet:
  //   And the bit after MSB is needed to handle overflow for adding two binary numbers.
  //   2 bit sign extension is necessary because the MSB of the 14-bit output indicates the sign bit of the significand. 
  //   Cin indicates the sign bit of A. So, when Cin=0, output of the ADDER is 0+A, otherwise output of the ADDER is 0-A i.e. A's 2's complement.
  //   Next the 12-bit output from the ADDER is extended by 2-bit in the MSB according to Cin or sign bit. Thus the final output is 14-bit.
  //   This circuit determines the two's complement of the given 12-bit input A, which is significand i.e. 1+fraction, and then sign extends the output by 2-bit. So the final output is 14-bit.
endmodule
