// Logisim project a1-g6-circuit.circ as structural Verilog: 1 circuit, main circuit main
module main (
  input  [15:0] in_1,
  input  [15:0] A,
  input  _4bit_Subt,
  input  [15:0] B,
  output [11:0] out_5,
  output out_6,
  output [11:0] out_7,
  output [11:0] out_8,
  output [11:0] out_9,
  output out_10,
  output [11:0] out_11,
  output [11:0] out_12,
  output [11:0] out_13,
  output out_14,
  output [3:0] out_15,
  output [3:0] out_16,
  output [15:0] F,
  output [3:0] out_18,
  output out_19,
  output out_20,
  output [3:0] out_21,
  output [3:0] out_22,
  output B_OR,
  output A_OR
);

  wire and_2_out, and_3_out, comparator_1_eq, comparator_1_gt, comparator_1_lt, not_1_out, not_2_out,
       or_5_out;
  wire [0:0] xor_1_out;
  wire [3:0] adder_4_out, multiplexer_1_out, multiplexer_2_out, multiplexer_5_out;
  wire [11:11] or_1_out, or_4_out, xor_2_out;
  wire [12:0] shifter_3_out;
  wire [12:12] shifter_2_out;
  wire [15:0] multiplexer_7_out;

  or or_1 (or_1_out[11], A[13], A[12], A[11], A[10]);
  or or_2 (B_OR, B[14], B[13], B[12], B[11], B[10], B[9], B[8], B[7], B[6], B[5], B[4], B[3], B[2], B[1], B[0]);
  or or_3 (A_OR, A[14], A[13], A[12], A[11], A[10], A[9], A[8], A[7], A[6], A[5], A[4], A[3], A[2], A[1], A[0]);
  or or_4 (or_4_out[11], B[13], B[12], B[11], B[10]);
  Multiplexer #(.width(4), .enable("false")) multiplexer_1 (
    .in0({3'b000, xor_1_out[0]}), .in1(A[14:11]), .out(multiplexer_1_out), .sel(or_1_out[11]));
  Comparator #(.width(4), .mode("unsigned")) comparator_1 (
    .a(multiplexer_1_out), .b(multiplexer_2_out), .gt(comparator_1_gt), .eq(comparator_1_eq),
    .lt(comparator_1_lt));
  Multiplexer #(.width(4), .enable("false")) multiplexer_2 (
    .in0({3'b000, xor_1_out[0]}), .in1(B[14:11]), .out(multiplexer_2_out), .sel(or_4_out[11]));
  or or_5 (or_5_out, comparator_1_gt, comparator_1_eq);
  Multiplexer #(.width(12), .enable("false")) multiplexer_3 (
    .in0({or_1_out[11], A[10:0]}), .in1({or_4_out[11], B[10:0]}), .out(out_8), .sel(comparator_1_lt));
  Multiplexer #(.width(12), .enable("false")) multiplexer_4 (
    .in0({or_1_out[11], A[10:0]}), .in1({or_4_out[11], B[10:0]}), .out(out_12), .sel(or_5_out));
  buf xor_1 (xor_1_out[0], or_1_out[11]);  // XOR_Gate
  Multiplexer #(.width(4), .enable("false")) multiplexer_5 (
    .in0(multiplexer_1_out), .in1(multiplexer_2_out), .out(multiplexer_5_out), .sel(or_5_out));
  Multiplexer #(.width(4), .enable("false")) multiplexer_6 (
    .in0(multiplexer_1_out), .in1(multiplexer_2_out), .out(out_22), .sel(comparator_1_lt));
  Subtractor #(.width(4)) subtractor_1 (.a(out_22), .b(multiplexer_5_out), .out(out_21), .bin(1'b0), .bout(_4bit_Subt));
  Shifter #(.width(12), .shift("lr")) shifter_1 (.in(out_12), .\dist (out_21), .out(out_13));
  Adder #(.width(12)) adder_1 (.a(out_8), .b(out_13), .out(out_9), .cin(1'b0), .cout(out_10));
  Adder #(.width(4)) adder_2 (.a({3'b000, out_10}), .b(out_22), .out(out_18), .cin(1'b0), .cout(out_19));
  and and_1 (out_6, out_10, out_9[0]);
  Shifter #(.width(13), .shift("lr")) shifter_2 (
    .in({out_10, out_9}), .\dist ({3'b000, out_10}), .out({shifter_2_out[12], out_11}));
  not not_1 (not_1_out, or_1_out[11]);
  not not_2 (not_2_out, or_4_out[11]);
  Adder #(.width(12)) adder_3 (.a({12{1'b0}}), .b(out_11), .out(out_5), .cin(out_6), .cout(out_14));
  and and_2 (and_2_out, or_1_out[11], not_2_out);
  buf and_3 (and_3_out, or_4_out[11]);  // AND_Gate
  // OR_Gate or_6 has open pins: in0=and_2_out, in1=and_3_out, out=open
  Adder #(.width(4)) adder_4 (.a({3'b000, out_14}), .b(out_18), .out(adder_4_out), .cin(1'b0), .cout(out_20));
  Shifter #(.width(13), .shift("lr")) shifter_3 (.in({out_14, out_5}), .\dist ({3'b000, out_14}), .out(shifter_3_out));
  xor xor_2 (xor_2_out[11], or_1_out[11], or_4_out[11]);
  Adder #(.width(16)) adder_5 (
    .a(multiplexer_7_out), .b({4'b0000, xor_2_out[11], {10{1'b0}}, xor_2_out[11]}), .out(F));  // open: cin, cout
  Multiplexer #(.select(2), .width(16), .enable("false")) multiplexer_7 (
    .in0(in_1), .in1(A), .in2(B), .in3({1'b0, adder_4_out, shifter_3_out[10:0]}), .out(multiplexer_7_out),
    .sel({B_OR, A_OR}));

  assign out_7 = {12{1'b0}};
  assign out_15 = {3'b000, out_14};
  assign out_16 = {3'b000, out_10};

  // Notes on the sheet:
  //   4bit Comp.
  //   4bit MUX
  //   4bit MUX
  //   12bit MUX
  //   larger
  //   12bit MUX
  //   smaller
  //   smaller
  //   larger
  //   12bit Shifter
  //   12bit Adder
  //   4bit Adder
  //   13bit Shifter
  //   12bit Adder
  //   4bit Adder
  //   13bit Shifter
endmodule
