// Logisim project 8 Bit Register.circ as structural Verilog
module _8_bit_register (
);

  Decoder #(.select(3)) decoder_1 ();  // open: out0, out1, out2, out3, out4, out5, out6, out7, sel, en
  Register register_1 ();  // open: D, en, Q, clk, clr
  Register register_2 ();  // open: D, en, Q, clk, clr
  Register register_3 ();  // open: D, en, Q, clk, clr
  Register register_4 ();  // open: D, en, Q, clk, clr
  Register register_5 ();  // open: D, en, Q, clk, clr
  Register register_6 ();  // open: D, en, Q, clk, clr
  Register register_7 ();  // open: D, en, Q, clk, clr
  Register register_8 ();  // open: D, en, Q, clk, clr
  Multiplexer #(.select(3), .width(8)) multiplexer_1 ();  // open: in0, in1, in2, in3, in4, in5, in6, in7, out, sel, en
  Multiplexer #(.select(3), .width(8)) multiplexer_2 ();  // open: in0, in1, in2, in3, in4, in5, in6, in7, out, sel, en
endmodule
