// Logisim project MIPS.circ as structural Verilog: 1 circuit, main circuit main
module main (
  output [11:0] out_1,
  output [19:0] out_2
);

  wire alu_1_p4, and_1_out, and_2_out, and_3_out, clock_1_out, multiplexer_5_out, not_1_out, not_2_out;
  wire [3:0] multiplexer_1_out, multiplexer_2_out;
  wire [7:0] adder_1_out, adder_2_out, alu_1_p5, bit_extender_1_out, multiplexer_3_out, multiplexer_4_out,
       multiplexer_6_out, multiplexer_7_out, multiplexer_8_out, ram_1_data, register_1_q,
       register_file_1_read_data_1, register_file_1_read_data_2;

  Clock clock_1 (.out(clock_1_out));
  Register register_1 (.D(multiplexer_8_out), .Q(register_1_q), .clk(clock_1_out));  // open: en, clr
  Adder adder_1 (.a(8'h1), .b(register_1_q), .out(adder_1_out));  // open: cin, cout
  ROM #(.dataWidth(20)) rom_1 (.addr(register_1_q), .data(out_2));  // open: sel
  assign bit_extender_1_out = {{4{1'b0}}, out_2[3:0]};  // Bit_Extender bit_extender_1
  Multiplexer #(.width(4), .enable("false")) multiplexer_1 (
    .in0(out_2[15:12]), .in1(out_2[11:8]), .out(multiplexer_1_out), .sel(and_3_out));
  Multiplexer #(.width(4), .enable("false")) multiplexer_2 (
    .in0(out_2[11:8]), .in1(out_2[7:4]), .out(multiplexer_2_out), .sel(out_1[10]));
  Multiplexer #(.width(8), .enable("false")) multiplexer_3 (
    .in0(out_2[7:0]), .in1(bit_extender_1_out), .out(multiplexer_3_out), .sel(and_3_out));
  ROM #(.addrWidth(4), .dataWidth(12)) rom_2 (.addr(out_2[19:16]), .data(out_1));  // open: sel
  Register_File register_file_1 (
    .Write_Data(multiplexer_7_out), .Read_Reg1(multiplexer_1_out), .Read_Reg2(out_2[11:8]),
    .Write_Reg(multiplexer_2_out), .Reg_clock(clock_1_out), .RegWrite(out_1[8]),
    .Read_Data_1(register_file_1_read_data_1), .Read_Data_2(register_file_1_read_data_2));  // open: Error_Write_to_0
  Multiplexer #(.width(8), .enable("false")) multiplexer_4 (
    .in0(register_file_1_read_data_2), .in1(multiplexer_3_out), .out(multiplexer_4_out), .sel(out_1[9]));
  // ALU alu_1: pin names not known; wires that end beside it: register_file_1_read_data_1, multiplexer_4_out, out_1[2:0], alu_1_p4, alu_1_p5
  Adder adder_2 (.a(adder_1_out), .b(multiplexer_3_out), .out(adder_2_out));  // open: cin, cout
  Multiplexer #(.enable("false")) multiplexer_5 (
    .in0(and_1_out), .in1(and_2_out), .out(multiplexer_5_out), .sel(out_1[4]));
  and and_1 (and_1_out, out_1[5], alu_1_p4);
  RAM #(.bus("separate")) ram_1 (
    .addr(alu_1_p5), .din(register_file_1_read_data_2), .data(ram_1_data), .str(out_1[6]), .clk(clock_1_out),
    .ld(out_1[7]));  // open: sel, clr
  Multiplexer #(.width(8), .enable("false")) multiplexer_6 (
    .in0(adder_1_out), .in1(adder_2_out), .out(multiplexer_6_out), .sel(multiplexer_5_out));
  and and_2 (and_2_out, out_1[5], not_1_out);
  not not_1 (not_1_out, alu_1_p4);
  Multiplexer #(.width(8), .enable("false")) multiplexer_7 (
    .in0(alu_1_p5), .in1(ram_1_data), .out(multiplexer_7_out), .sel(out_1[11]));
  Multiplexer #(.width(8), .enable("false")) multiplexer_8 (
    .in0(multiplexer_6_out), .in1(out_2[7:0]), .out(multiplexer_8_out), .sel(out_1[3]));
  not not_2 (not_2_out, out_1[5]);
  and and_3 (and_3_out, not_2_out, out_1[4]);

  // Notes on the sheet:
  //   contents of rom_1 (hex, n*v repeats v):
  //   777ff 834fc 73338 43420 d2310 b3538 65150 33438 f3420 54420 93200 a530a 32a 75508 e0542
  //   RegWrite
  //   contents of rom_2 (hex, n*v repeats v):
  //   715 21 31 302 500 504 503 300 301 240 b80 303 f 501 716 502
  //   RegDst
  //   ALUOp
  //   ALUSrc
  //   Jump
  //   BSC
  //   Branch
  //   MemToReg
  //   MemWrite
  //   MemRead
  //   Branch'
  //   BSC
endmodule
