// Logisim project Register file.circ as structural Verilog
module Register_File (
  input  [7:0] Write_Data,
  input  [7:0] Init_tWrite_Data,
  input  [3:0] Read_Reg1,
  input  [3:0] Read_Reg2,
  input  [3:0] Write_Reg,
  input  [3:0] init_Write_Reg,
  input  Reg_clock,
  input  Init_Reg_clock,
  input  Init_Reg_clock_2,
  input  reg_init,
  input  RegWrite,
  output [7:0] Read_Data_1,
  output [7:0] Read_Data_2,
  output Error_Write_to_0
);

  wire and_2_out, and_3_out, and_4_out, and_5_out, and_6_out, and_7_out, and_8_out, decoder_1_out0,
       decoder_1_out1, decoder_1_out2, decoder_1_out3, decoder_1_out4, decoder_1_out5, decoder_1_out6,
       decoder_1_out7, multiplexer_3_out, multiplexer_4_out;
  wire [3:0] multiplexer_2_out;
  wire [7:0] multiplexer_1_out, register_1_q, register_2_q, register_3_q, register_4_q, register_5_q,
       register_6_q, register_7_q, register_8_q;

  Multiplexer #(.width(8), .disabled(0), .enable("false")) multiplexer_1 (
    .in0(Write_Data), .in1(Init_tWrite_Data), .out(multiplexer_1_out), .sel(reg_init));
  Multiplexer #(.width(4), .disabled(0), .enable("false")) multiplexer_2 (
    .in0(Write_Reg), .in1(init_Write_Reg), .out(multiplexer_2_out), .sel(reg_init));
  Decoder #(.select(4), .enable("false")) decoder_1 (
    .out0(decoder_1_out0), .out1(decoder_1_out1), .out2(decoder_1_out2), .out3(decoder_1_out3),
    .out4(decoder_1_out4), .out5(decoder_1_out5), .out6(decoder_1_out6), .out7(decoder_1_out7),
    .sel(multiplexer_2_out));  // open: out8, out9, out10, out11, out12, out13, out14, out15
  Multiplexer #(.disabled(0), .enable("false")) multiplexer_3 (
    .in0(Reg_clock), .in1(Init_Reg_clock), .out(multiplexer_3_out), .sel(reg_init));
  Multiplexer #(.disabled(0), .enable("false")) multiplexer_4 (
    .in0(RegWrite), .in1(reg_init), .out(multiplexer_4_out), .sel(reg_init));
  and and_1 (Error_Write_to_0, decoder_1_out0, multiplexer_4_out);
  and and_2 (and_2_out, decoder_1_out1, multiplexer_4_out);
  and and_3 (and_3_out, decoder_1_out2, multiplexer_4_out);
  and and_4 (and_4_out, decoder_1_out3, multiplexer_4_out);
  and and_5 (and_5_out, decoder_1_out4, multiplexer_4_out);
  and and_6 (and_6_out, decoder_1_out5, multiplexer_4_out);
  and and_7 (and_7_out, decoder_1_out6, multiplexer_4_out);
  and and_8 (and_8_out, decoder_1_out7, multiplexer_4_out);
  Register register_1 (.D(multiplexer_1_out), .Q(register_1_q));  // open: en, clk, clr
  Register register_2 (.D(multiplexer_1_out), .en(and_2_out), .Q(register_2_q), .clk(multiplexer_3_out));  // open: clr
  Register register_3 (.D(multiplexer_1_out), .en(and_3_out), .Q(register_3_q), .clk(multiplexer_3_out));  // open: clr
  Register register_4 (.D(multiplexer_1_out), .en(and_4_out), .Q(register_4_q), .clk(multiplexer_3_out));  // open: clr
  Register register_5 (.D(multiplexer_1_out), .en(and_5_out), .Q(register_5_q), .clk(multiplexer_3_out));  // open: clr
  Register register_6 (.D(multiplexer_1_out), .en(and_6_out), .Q(register_6_q), .clk(multiplexer_3_out));  // open: clr
  Register register_7 (.D(multiplexer_1_out), .en(and_7_out), .Q(register_7_q), .clk(multiplexer_3_out));  // open: clr
  Register register_8 (.D(multiplexer_1_out), .en(and_8_out), .Q(register_8_q), .clk(multiplexer_3_out));  // open: clr
  Multiplexer #(.select(4), .width(8), .enable("false")) multiplexer_5 (
    .in0(register_1_q), .in1(register_2_q), .in2(register_3_q), .in3(register_4_q), .in4(register_5_q),
    .in5(register_6_q), .in6(register_7_q), .in7(register_8_q), .out(Read_Data_1), .sel(Read_Reg1));  // open: in8, in9, in10, in11, in12, in13, in14, in15
  Multiplexer #(.select(4), .width(8), .enable("false")) multiplexer_6 (
    .in0(register_1_q), .in1(register_2_q), .in2(register_3_q), .in3(register_4_q), .in4(register_5_q),
    .in5(register_6_q), .in6(register_7_q), .in7(register_8_q), .in8(register_8_q), .out(Read_Data_2),
    .sel(Read_Reg2));  // open: in9, in10, in11, in12, in13, in14, in15

  assign Init_Reg_clock_2 = Init_Reg_clock;
endmodule
