// Logisim project Pipelining.circ as structural Verilog: 4 circuits, main circuit main
module main (
  input  Reg_INIT,
  input  Reg_INIT_clock,
  input  [3:0] Reg_INIT_num,
  input  [7:0] Reg_INIT_data,
  output [7:0] out_5,
  output [7:0] out_6,
  output [7:0] out_7,
  output [7:0] out_8,
  output [7:0] out_9
);

  wire clock_1_out;
  wire [1:0] forwarding_unit_1_forwarda, forwarding_unit_1_forwardb, register_4_q, register_10_q;
  wire [2:0] register_3_q;
  wire [3:0] register_7_q, register_8_q, register_9_q, register_13_q, register_15_q;
  wire [7:0] adder_1_out, alu_1_f, multiplexer_1_out, multiplexer_2_out, register_1_q, register_5_q,
       register_6_q, register_11_q, register_12_q, register_14_q, register_file_1_read_data_1,
       register_file_1_read_data_2;
  wire [11:0] rom_2_data;
  wire [19:0] register_2_q, rom_1_data;

  Clock clock_1 (.out(clock_1_out));
  Register #(.trigger("falling")) register_1 (.D(adder_1_out), .Q(register_1_q), .clk(clock_1_out));  // open: en, clr
  Adder adder_1 (.a(8'h1), .b(register_1_q), .out(adder_1_out));  // open: cin, cout
  ROM #(.dataWidth(20)) rom_1 (.addr(register_1_q), .data(rom_1_data));  // open: sel
  Register #(.width(20)) register_2 (.D(rom_1_data), .Q(register_2_q), .clk(clock_1_out));  // open: en, clr
  ROM #(.addrWidth(4), .dataWidth(12)) rom_2 (.addr(register_2_q[19:16]), .data(rom_2_data));  // open: sel
  Register_File register_file_1 (
    .Write_Data(register_14_q), .Init_tWrite_Data(Reg_INIT_data), .t0(out_5),
    .Read_Reg1(register_2_q[15:12]), .t1(out_6), .t2(out_7), .t3(out_8), .t4(out_9),
    .Read_Reg2(register_2_q[11:8]), .Write_Reg(register_15_q), .init_Write_Reg(Reg_INIT_num),
    .Reg_clock(clock_1_out), .Init_Reg_clock(Reg_INIT_clock), .reg_init(Reg_INIT), .RegWrite(rom_2_data[8]),
    .Read_Data_1(register_file_1_read_data_1), .Read_Data_2(register_file_1_read_data_2));  // open: out_17, out_18, Error_Write_to_0
  Register #(.width(3)) register_3 (.D(rom_2_data[2:0]), .Q(register_3_q), .clk(clock_1_out));  // open: en, clr
  Register #(.width(2)) register_4 (.D(rom_2_data[7:6]), .Q(register_4_q), .clk(clock_1_out));  // open: en, clr
  Register register_5 (.D(register_file_1_read_data_1), .Q(register_5_q), .clk(clock_1_out));  // open: en, clr
  Register register_6 (.D(register_file_1_read_data_2), .Q(register_6_q), .clk(clock_1_out));  // open: en, clr
  Register #(.width(4)) register_7 (.D(register_2_q[7:4]), .Q(register_7_q), .clk(clock_1_out));  // open: en, clr
  Register #(.width(4)) register_8 (.D(register_2_q[15:12]), .Q(register_8_q), .clk(clock_1_out));  // open: en, clr
  Register #(.width(4)) register_9 (.D(register_2_q[11:8]), .Q(register_9_q), .clk(clock_1_out));  // open: en, clr
  Multiplexer #(.select(2), .width(8), .enable("false")) multiplexer_1 (
    .in0(register_5_q), .in1(register_14_q), .in2(register_11_q), .out(multiplexer_1_out),
    .sel(forwarding_unit_1_forwarda));  // open: in3
  Multiplexer #(.select(2), .width(8), .enable("false")) multiplexer_2 (
    .in0(register_6_q), .in1(register_14_q), .in2(register_11_q), .out(multiplexer_2_out),
    .sel(forwarding_unit_1_forwardb));  // open: in3
  Forwarding_Unit forwarding_unit_1 (
    .ID_EX_RS(register_8_q), .ID_EX_RT(register_9_q), .EX_MEM_RegWrite(1'b1), .EX_MEM_RegRd(register_13_q),
    .MEM___WB_RegWrite(1'b1), .MEM_WB_RegRd(register_15_q), .ForwardA(forwarding_unit_1_forwarda),
    .ForwardB(forwarding_unit_1_forwardb));
  Register #(.width(2)) register_10 (.D(register_4_q), .Q(register_10_q), .clk(clock_1_out));  // open: en, clr
  Register register_11 (.D(alu_1_f), .Q(register_11_q), .clk(clock_1_out));  // open: en, clr
  ALU alu_1 (
    .A(multiplexer_1_out), .B(multiplexer_2_out), .ALUop(register_3_q), .F(alu_1_f));  // open: overflow, negative, ZF
  Register register_12 (.D(register_6_q), .Q(register_12_q), .clk(clock_1_out));  // open: en, clr
  Register #(.width(4)) register_13 (.D(register_7_q), .Q(register_13_q), .clk(clock_1_out));  // open: en, clr
  RAM #(.bus("separate")) ram_1 (
    .addr(register_11_q), .din(register_12_q), .str(register_10_q[0]), .clk(clock_1_out),
    .ld(register_10_q[1]));  // open: data, sel, clr
  Register register_14 (.D(register_11_q), .Q(register_14_q), .clk(clock_1_out));  // open: en, clr
  Register #(.width(4)) register_15 (.D(register_13_q), .Q(register_15_q), .clk(clock_1_out));  // open: en, clr

  // Other names for the same wires on the sheet: t0[7:0] = out_5; t1[7:0] = out_6; t2[7:0] = out_7; t3[7:0] = out_8;
  //   t4[7:0] = out_9

  // Notes on the sheet:
  //   contents of rom_1 (hex, n*v repeats v):
  //   43420 d2350 f2450 42550
  //   IF/ID
  //   Instruction
  //   contents of rom_2 (hex, n*v repeats v):
  //   f05 31 21 302 500 504 503 300 301 240 380 303 f 501 f06 502
  //   RegWrite
  //   ID/EX
  //   ALUOp
  //   MemWrite/MemRead
  //   rs data
  //   rt data
  //   rd
  //   rs
  //   rt
  //   ForwardA
  //   ID/EX.rs
  //   ID/EX.rt
  //   ForwardB
  //   EX/MEM
  //   MemWrite/MemRead
  //   ALU Result
  //   rt data
  //   rd
  //   Forwarding Unit
  //   EX/MEM rd
  //   MEM/WB rd
  //   MemWrite
  //   MemRead
  //   MEM/WB
  //   ALU Result from EX/MEM
  //   rd from EX/MEM
endmodule

module Forwarding_Unit (
  input  [3:0] ID_EX_RS,
  input  [3:0] ID_EX_RT,
  input  EX_MEM_RegWrite,
  input  [3:0] EX_MEM_RegRd,
  input  MEM___WB_RegWrite,
  input  [3:0] MEM_WB_RegRd,
  output [1:0] ForwardA,
  output [1:0] ForwardB
);

  wire comparator_1_eq, comparator_2_eq, comparator_3_eq, comparator_4_eq, comparator_5_eq, comparator_6_eq,
       comparator_7_eq, comparator_8_eq, not_1_out, not_2_out, not_3_out, not_4_out, not_5_out, not_6_out;

  Comparator #(.width(4)) comparator_1 (.a(EX_MEM_RegRd), .b(4'b0000), .eq(comparator_1_eq));  // open: gt, lt
  Comparator #(.width(4)) comparator_2 (.a(EX_MEM_RegRd), .b(ID_EX_RS), .eq(comparator_2_eq));  // open: gt, lt
  Comparator #(.width(4)) comparator_3 (.a(ID_EX_RS), .b(MEM_WB_RegRd), .eq(comparator_3_eq));  // open: gt, lt
  Comparator #(.width(4)) comparator_4 (.a(MEM_WB_RegRd), .b(4'b0000), .eq(comparator_4_eq));  // open: gt, lt
  Comparator #(.width(4)) comparator_5 (.a(EX_MEM_RegRd), .b(ID_EX_RT), .eq(comparator_5_eq));  // open: gt, lt
  Comparator #(.width(4)) comparator_6 (.a(EX_MEM_RegRd), .b(4'b0000), .eq(comparator_6_eq));  // open: gt, lt
  Comparator #(.width(4)) comparator_7 (.a(MEM_WB_RegRd), .b(ID_EX_RT), .eq(comparator_7_eq));  // open: gt, lt
  Comparator #(.width(4)) comparator_8 (.a(MEM_WB_RegRd), .b(4'b0000), .eq(comparator_8_eq));  // open: gt, lt
  not not_1 (not_1_out, comparator_1_eq);
  not not_2 (not_2_out, comparator_4_eq);
  not not_3 (not_3_out, comparator_6_eq);
  not not_4 (not_4_out, ForwardB[1]);
  not not_5 (not_5_out, comparator_8_eq);
  not not_6 (not_6_out, ForwardA[1]);
  and and_1 (ForwardB[1], EX_MEM_RegWrite, comparator_5_eq, not_3_out);
  and and_2 (ForwardB[0], not_4_out, comparator_7_eq, not_5_out, MEM___WB_RegWrite);
  and and_3 (ForwardA[1], EX_MEM_RegWrite, not_1_out, comparator_2_eq);
  and and_4 (ForwardA[0], not_6_out, MEM___WB_RegWrite, comparator_3_eq, not_2_out);
endmodule

module Register_File (
  input  [7:0] Write_Data,
  input  [7:0] Init_tWrite_Data,
  input  [3:0] Read_Reg1,
  input  [3:0] Read_Reg2,
  input  [3:0] Write_Reg,
  input  [3:0] init_Write_Reg,
  input  Reg_clock,
  input  Init_Reg_clock,
  input  reg_init,
  input  RegWrite,
  output [7:0] t0,
  output [7:0] t1,
  output [7:0] t2,
  output [7:0] t3,
  output [7:0] Read_Data_1,
  output [7:0] t4,
  output [7:0] out_17,
  output [7:0] out_18,
  output [7:0] Read_Data_2,
  output Error_Write_to_0
);

  wire and_2_out, and_3_out, and_4_out, and_5_out, and_6_out, and_7_out, and_8_out, decoder_1_out0,
       decoder_1_out1, decoder_1_out2, decoder_1_out3, decoder_1_out4, decoder_1_out5, decoder_1_out6,
       decoder_1_out7, multiplexer_3_out, multiplexer_4_out;
  wire [3:0] multiplexer_2_out;
  wire [7:0] multiplexer_1_out, register_1_q;

  Multiplexer #(.width(8), .disabled(0), .enable("false")) multiplexer_1 (
    .in0(Write_Data), .in1(Init_tWrite_Data), .out(multiplexer_1_out), .sel(reg_init));
  Multiplexer #(.width(4), .disabled(0), .enable("false")) multiplexer_2 (
    .in0(Write_Reg), .in1(init_Write_Reg), .out(multiplexer_2_out), .sel(reg_init));
  Decoder #(.select(4), .enable("false")) decoder_1 (
    .out0(decoder_1_out0), .out1(decoder_1_out1), .out2(decoder_1_out2), .out3(decoder_1_out3),
    .out4(decoder_1_out4), .out5(decoder_1_out5), .out6(decoder_1_out6), .out7(decoder_1_out7),
    .sel(multiplexer_2_out));  // open: out8, out9, out10, out11, out12, out13, out14, out15
  Multiplexer #(.disabled(0), .enable("false")) multiplexer_3 (
    .in0(Reg_clock), .in1(Init_Reg_clock), .out(multiplexer_3_out), .sel(reg_init));
  Multiplexer #(.disabled(0), .enable("false")) multiplexer_4 (
    .in0(RegWrite), .in1(reg_init), .out(multiplexer_4_out), .sel(reg_init));
  and and_1 (Error_Write_to_0, decoder_1_out0, multiplexer_4_out);
  and and_2 (and_2_out, decoder_1_out1, multiplexer_4_out);
  and and_3 (and_3_out, decoder_1_out2, multiplexer_4_out);
  and and_4 (and_4_out, decoder_1_out3, multiplexer_4_out);
  and and_5 (and_5_out, decoder_1_out4, multiplexer_4_out);
  and and_6 (and_6_out, decoder_1_out5, multiplexer_4_out);
  and and_7 (and_7_out, decoder_1_out6, multiplexer_4_out);
  and and_8 (and_8_out, decoder_1_out7, multiplexer_4_out);
  Register register_1 (.D(multiplexer_1_out), .Q(register_1_q));  // open: en, clk, clr
  Register #(.trigger("falling")) register_2 (
    .D(multiplexer_1_out), .en(and_2_out), .Q(t0), .clk(multiplexer_3_out));  // open: clr
  Register #(.trigger("falling")) register_3 (
    .D(multiplexer_1_out), .en(and_3_out), .Q(t1), .clk(multiplexer_3_out));  // open: clr
  Register #(.trigger("falling")) register_4 (
    .D(multiplexer_1_out), .en(and_4_out), .Q(t2), .clk(multiplexer_3_out));  // open: clr
  Register #(.trigger("falling")) register_5 (
    .D(multiplexer_1_out), .en(and_5_out), .Q(t3), .clk(multiplexer_3_out));  // open: clr
  Register #(.trigger("falling")) register_6 (
    .D(multiplexer_1_out), .en(and_6_out), .Q(t4), .clk(multiplexer_3_out));  // open: clr
  Register #(.trigger("falling")) register_7 (
    .D(multiplexer_1_out), .en(and_7_out), .Q(out_17), .clk(multiplexer_3_out));  // open: clr
  Register #(.trigger("falling")) register_8 (
    .D(multiplexer_1_out), .en(and_8_out), .Q(out_18), .clk(multiplexer_3_out));  // open: clr
  Multiplexer #(.select(4), .width(8), .enable("false")) multiplexer_5 (
    .in0(register_1_q), .in1(t0), .in2(t1), .in3(t2), .in4(t3), .in5(t4), .in6(out_17), .in7(out_18),
    .out(Read_Data_1), .sel(Read_Reg1));  // open: in8, in9, in10, in11, in12, in13, in14, in15
  Multiplexer #(.select(4), .width(8), .enable("false")) multiplexer_6 (
    .in0(register_1_q), .in1(t0), .in2(t1), .in3(t2), .in4(t3), .in5(t4), .in6(out_17), .in7(out_18),
    .in8(out_18), .out(Read_Data_2), .sel(Read_Reg2));  // open: in9, in10, in11, in12, in13, in14, in15

  // Other names for the same wires on the sheet: sp[7:0] = out_18; t5[7:0] = out_17
endmodule

module ALU (
  input  [7:0] A,
  input  [7:0] B,
  input  [2:0] ALUop,
  output overflow,
  output ZF,
  output negative,
  output [7:0] F
);

  wire [7:0] adder_1_out, and_1_out, nor_1_out, or_1_out, subtractor_1_out;
  wire [15:0] shifter_1_out, shifter_2_out;

  Adder adder_1 (.a(A), .b(B), .out(adder_1_out), .cin(1'b0), .cout(overflow));
  Subtractor subtractor_1 (.a(A), .b(B), .out(subtractor_1_out), .bin(1'b0), .bout(negative));
  assign or_1_out = A | B;  // OR_Gate or_1, 8 bits wide
  assign and_1_out = A & B;  // AND_Gate and_1, 8 bits wide
  assign nor_1_out = ~(A | B);  // NOR_Gate nor_1, 8 bits wide
  Shifter #(.width(16)) shifter_1 (.in({{8{1'b0}}, A}), .\dist (B[3:0]), .out(shifter_1_out));
  Shifter #(.width(16), .shift("lr")) shifter_2 (.in({{8{1'b0}}, A}), .\dist (B[3:0]), .out(shifter_2_out));
  Multiplexer #(.select(3), .width(8), .enable("false")) multiplexer_1 (
    .in0(adder_1_out), .in1(subtractor_1_out), .in2(or_1_out), .in3(and_1_out), .in4(nor_1_out),
    .in5(shifter_1_out[7:0]), .in6(shifter_2_out[7:0]), .in7({8{1'b0}}), .out(F), .sel(ALUop));
  nor nor_2 (ZF, F[0], F[1], F[2], F[3], F[4], F[5], F[6], F[7]);
endmodule
